// Logisim project Circuit1 Logism.circ as structural Verilog: 1 circuit, main circuit main
module main (
  input  A,
  input  B,
  input  C,
  output out_4
);

  wire A_prime_B_prime_C_out, A_prime_BC_out, A_prime_out, AB_prime_C_out, AB_prime_C_prime_out, ABC_out,
       B_prime_out, C_prime_out;

  not A_prime (A_prime_out, A);
  not B_prime (B_prime_out, B);
  not C_prime (C_prime_out, C);
  and A_prime_BC (A_prime_BC_out, A_prime_out, B, C);
  and ABC (ABC_out, A, B, C);
  and AB_prime_C_prime (AB_prime_C_prime_out, A, B_prime_out, C_prime_out);
  and AB_prime_C (AB_prime_C_out, A, B_prime_out, C);
  and A_prime_B_prime_C (A_prime_B_prime_C_out, A_prime_out, B_prime_out, C);
  or f (out_4, A_prime_B_prime_C_out, A_prime_BC_out, ABC_out, AB_prime_C_out, AB_prime_C_prime_out);
endmodule
