// Logisim project Circuit_2_Logism.circ as structural Verilog: 1 circuit, main circuit main
module main (
  input  A,
  input  B,
  input  C,
  output out_4
);

  wire A_prime_B_prime_C_out, A_prime_BC_out, AB_prime_C_out, AB_prime_C_prime_out, ABC_out, not_1_out,
       not_2_out, not_3_out;

  not not_1 (not_1_out, A);
  not not_2 (not_2_out, B);
  not not_3 (not_3_out, C);
  nand A_prime_BC (A_prime_BC_out, not_1_out, B, C);
  nand ABC (ABC_out, A, B, C);
  nand AB_prime_C_prime (AB_prime_C_prime_out, A, not_2_out, not_3_out);
  nand A_prime_B_prime_C (A_prime_B_prime_C_out, not_1_out, not_2_out, C);
  nand AB_prime_C (AB_prime_C_out, A, not_2_out, C);
  nand f (out_4, A_prime_BC_out, A_prime_B_prime_C_out, ABC_out, AB_prime_C_out, AB_prime_C_prime_out);
endmodule
